# Fritzing sketch hbridge_ot (saved by Fritzing 1.0.2b)
breadboards: 1

parts:
  M1 = Arduino NANO RP2040 CONNECT with headers
  Part1 = Motor Driver 1A Dual TB6612FNG  # not connected
  M2 = gear-motor  # not connected
  M3 = gear-motor  # not connected
  R1 = Rotary Potentiometer (Small) [maximum_resistance=100kΩ knob_status=50% power=0.5W package=THT]

nets:
  N1: M1.GND-4, M1.GND-29, R1.leg1
  N2: M1.+3V3, R1.leg2
  N3: M1.D14, R1.wiper
