# Fritzing sketch pwm_led (saved by Fritzing 1.0.2b)
breadboards: 1

parts:
  M1 = Arduino NANO RP2040 CONNECT with headers
  LED1 = LED - 5mm [color="Red (633nm)" current=0.030A package="5 mm [THT]"]
  R1 = Resistor [tolerance=±5% resistance=220 package="1206 [SMD]"]
  U2 = POT [knob_status=50% power=0.5W package=pot_mammoth]

nets:
  N1: M1.GND-4, M1.GND-29, R1.Pin_1, U2.S
  N2: M1.D5, LED1.anode
  N3: M1.+3V3, U2.E
  N4: M1.D14, U2.A
  N5: LED1.cathode, R1.Pin_0
