# Fritzing sketch pwm_led_tof (saved by Fritzing 1.0.2b)
breadboards: 1

parts:
  M1 = Arduino NANO RP2040 CONNECT with headers
  LED1 = LED - 5mm [color="Red (633nm)" current=0.030A package="5 mm [THT]"]
  R1 = Resistor [tolerance=±5% resistance=220 package="1206 [SMD]"]
  Part1 = Adafruit VL530X Time of Flight Distance Sensor [part_number="Adafruit #3317"]

nets:
  N1: M1.GND-4, M1.GND-29, R1.Pin_1, Part1.GND
  N2: M1.D5, LED1.anode
  +3V3: M1.+3V3, Part1.VCC
  N3: M1.D18, Part1.SDA
  N4: M1.D19, Part1.SCL
  N5: LED1.cathode, R1.Pin_0

custom parts:
  Adafruit VL530X Time of Flight Distance Sensor: The VL53L0X is a Time of Flight distance sensor like no other you've used! The sensor contains a very tiny invisible laser source, and a matching sensor. The VL53L0X can detect the "time of flight", or how long the light has taken to bounce back to the sensor. Since it uses a very narrow light source, it is good for determining distance of only the surface directly in front of it. Unlike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
