# Fritzing sketch pwm_pot (saved by Fritzing 1.0.2b)
breadboards: 1

parts:
  M1 = Arduino NANO RP2040 CONNECT with headers
  U1 = POT [knob_status=50% power=0.5W package=pot_mammoth]
  J2 = Basic Servo

nets:
  N1: M1.GND-4, M1.GND-29, U1.S, J2.gnd
  N2: M1.D9, J2.pulse
  N3: M1.+3V3, U1.E
  N4: M1.D14, U1.A
  VIN: M1.VIN, J2.vcc
