# Fritzing sketch servo_pot (saved by Fritzing 1.0.2b)
breadboards: 1

parts:
  M1 = Arduino NANO RP2040 CONNECT with headers
  Q1 = TRANSISTOR_NPN [package=to-92]
  M3 = gear-motor
  U1 = POT [knob_status=50% power=0.5W package=pot_mammoth]

nets:
  N1: M1.GND-4, M1.GND-29, Q1.E, U1.S
  N2: M1.D2, Q1.B
  N3: M1.+3V3, U1.E
  N4: M1.D14, U1.A
  N5: M1.VIN, M3.pin_2
  N6: Q1.C, M3.pin_1
