# Fritzing sketch servo_sweep (saved by Fritzing 1.0.2b)
breadboards: 1

parts:
  M1 = Arduino NANO RP2040 CONNECT with headers
  J1 = Basic Servo

nets:
  N1: M1.GND-4, M1.GND-29, J1.gnd
  N2: M1.D9, J1.pulse
