# Fritzing sketch simple_dc_hbridge (saved by Fritzing 1.0.2b)
breadboards: 1

parts:
  M1 = Arduino NANO RP2040 CONNECT with headers
  Part1 = Motor Driver 1A Dual TB6612FNG  # not connected

nets:
  N1: M1.GND-4, M1.GND-29
