# Fritzing sketch solenoid (saved by Fritzing 1.0.2b)
breadboards: 1

parts:
  M1 = Arduino NANO RP2040 CONNECT with headers
  S3 = Pushbutton [package="[THT]"]
  Q1 = TRANSISTOR_NPN [package=to-92-ammo]
  R1 = Resistor [tolerance=±5% resistance=1k package="0805 [SMD]"]
  D1 = Schottky Diode [part_number=1N5817 package="Melf DO-213 AB [SMD]"]
  L1 = Solenoid
  Power_plug1 = Power plug

nets:
  N1: M1.GND-4, M1.GND-29, S3.Pin_3, Q1.E, Power_plug1.GND
  N2: M1.D2, R1.Pin_1
  N3: M1.D3, S3.Pin_1, S3.Pin_2
  N4: Q1.B, R1.Pin_0
  N5: Q1.C, D1.anode, L1.pin1
  N6: D1.cathode, L1.pin2, Power_plug1.VCC
