# Fritzing sketch stepper (saved by Fritzing 1.0.2b)
breadboards: 1

parts:
  M1 = Arduino NANO RP2040 CONNECT with headers
  Part1 = Motor Driver 1A Dual TB6612FNG  # not connected
  M2 = Stepper Motor - Bipolar  # not connected
  S3 = Pushbutton [package="[THT]"]
  S4 = Pushbutton [package="[THT]"]

nets:
  N1: M1.GND-4, M1.GND-29, S3.Pin_3, S3.Pin_4, S4.Pin_3, S4.Pin_4
  N2: M1.D11, S3.Pin_1, S3.Pin_2
  N3: M1.D12, S4.Pin_1, S4.Pin_2
