# Fritzing sketch tone (saved by Fritzing 1.0.2b)
breadboards: 1

parts:
  M1 = Arduino NANO RP2040 CONNECT with headers
  R1 = Resistor [tolerance=±5% power=0.25W resistance=100 package=THT]
  SP1 = SPEAKER [package=pcb_mount_speaker]

nets:
  N1: M1.GND-4, M1.GND-29, SP1.+
  N2: M1.D8, R1.Pin_0
  N3: R1.Pin_1, SP1.-
