# Fritzing sketch tone_fsr (saved by Fritzing 1.0.2b)
breadboards: 1

parts:
  M1 = Arduino NANO RP2040 CONNECT with headers
  R1 = Resistor [tolerance=±5% power=0.25W resistance=100 package=THT]
  SP1 = SPEAKER [package=pcb_mount_speaker]
  R2 = Basic Force Sensing Resistor (FSR) [package=THT]
  R3 = Resistor [tolerance=±5% resistance=10k package="1206 [SMD]"]
  R4 = Basic Force Sensing Resistor (FSR) [package=THT]
  R5 = Basic Force Sensing Resistor (FSR) [package=THT]
  R6 = Resistor [tolerance=±5% resistance=10k package="1206 [SMD]"]
  R7 = Resistor [tolerance=±5% resistance=10k package="1206 [SMD]"]

nets:
  N1: M1.GND-4, M1.GND-29, SP1.+, R3.Pin_1, R6.Pin_1, R7.Pin_1
  N2: M1.D8, R1.Pin_0
  N3: M1.+3V3, R2.pin_1, R4.pin_1, R5.pin_1
  N4: M1.D14, R5.pin_2, R7.Pin_0
  N5: M1.D15, R4.pin_2, R6.Pin_0
  N6: M1.D16, R2.pin_2, R3.Pin_0
  N7: R1.Pin_1, SP1.-
